# Fritzing sketch cloudSmoker (saved by Fritzing 0.9.6b)
stripboards: 1

parts:
  U1 = NodeMCU V1.0
  Part2 = Adafruit ADS1015 12Bit I2C ADC [part_number="Adafruit #1083"]
  Display1 = LCD screen 16x2 IIC [part_number=101290]
  TRS1 = SUYIN Audio Jack (TRS) 3.5mm [package="SUYIN [THT]"]
  TRS2 = SUYIN Audio Jack (TRS) 3.5mm [package="SUYIN [THT]"]
  J1 = male pin header, 5 pins [form="♂ (male)"]
  C1 = Ceramic Capacitor [capacitance=100nF voltage=35V package="100 mil [THT, multilayer]"]
  R1 = Vertical Resistor [tolerance=±20% resistance=100k package=THT]
  R2 = Vertical Resistor [tolerance=±20% resistance=100k package=THT]
  C2 = Ceramic Capacitor [capacitance=100nF voltage=35V package="100 mil [THT, multilayer]"]
  R4 = Resistor [tolerance=±1% power=0.25 resistance=75k package=THT]
  R3 = Resistor [tolerance=±1% power=0.25 resistance=9.09k package=THT]
  R5 = Resistor [tolerance=±5% power=0.25 resistance=10k package=THT]
  R6 = Resistor [tolerance=±5% power=0.25 resistance=10k package=THT]
  C3 = Electrolytic Capacitor [capacitance=0.47mF voltage=35V package="300 mil [THT, electrolytic]"]
  J2 = male alternating pin header, 4 pins [form="♂ (male)"]
  V1 = DC Power [voltage=5]
  ENCODER1 = Rotary Encoder with switch (KY-040) [part_number=KY-040]

nets:
  SCL: U1.D1, Part2.SCL, Display1.SCL, R6.Pin_1, J2.pin1
  N1: U1.D2, Part2.SDA, Display1.SDA, R5.Pin_1, J2.pin2
  SW: U1.D3, J1.pin3, ENCODER1.SW
  DT: U1.D4, J1.pin2, ENCODER1.DT
  GND: U1.GND, U1.RST, Part2.GND, Display1.GND, TRS1.Sleeve, TRS1.Ring, TRS2.Sleeve, TRS2.Ring, J1.pin5, C1.1, C2.0, C3.-, J2.pin4, V1.V-, ENCODER1.GND
  CLK: U1.D5, J1.pin1, ENCODER1.CLK
  5V: U1.Vin, Part2.AIN0, Part2.VDD, Display1.VCC, J1.pin4, R4.Pin_1, R3.Pin_1, R5.Pin_0, R6.Pin_0, C3.+, J2.pin3, V1.V+, ENCODER1.+
  N2: Part2.AIN3, R2.Pin_1
  N3: Part2.AIN2, R1.Pin_1
  N4: TRS1.Tip, C1.0, R1.Pin_0, R4.Pin_0
  N5: TRS2.Tip, R2.Pin_0, C2.1, R3.Pin_0

notes:
  SW
  DT
  CLK
  SCL
  SDA
  pitProbe
  meatProbe

custom parts:
  NodeMCU V1.0: ESP8266 based NodeMCU
  Adafruit ADS1015 12Bit I2C ADC: For microcontrollers without an analog-to-digital converter or when you want a higher-precision ADC, the ADS1015 provides 12-bit precision at 3300 samples/second over I2C. The chip can be configured as 4 single-ended input channels, or two differential channels. As a nice bonus, it even includes a programmable gain amplifier, up to x16, to help boost up smaller single/differential signals to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
  LCD screen 16x2 IIC: LCD screen with HD44780 controller enables showing text, symbols, value or anything else that comes from Croduino/Arduino. It is capable of showing 16 symbols in two lines and therefore can be used in many projects that need to send clearly visible and legible output information.. • Color of symbols: White • Backlight: Blue • Dimensions: 80 x 36 x 12 mm • Screen dimensions: 64.5 x 16 mm •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
  SUYIN Audio Jack (TRS) 3.5mm: Stereo Jack 3.5mm
  Vertical Resistor: A generic resistor (0.25W)
  Rotary Encoder with switch (KY-040): A Rotary Encoder with switch
